// Digital circuit 0 to 5 counter.dig as structural Verilog
module _0_to_5_counter (
  input  CLK,
  output [3:0] Output
);

  CounterPreset #(.maxValue(5), .Bits(4), .isProgramCounter("true")) counterpreset_1 (
    .en(~1'b0), .C(CLK), .dir(1'b0), .in(4'b0000), .ld(1'b0), .clr(1'b0), .out(Output));  // open: ovf
endmodule
