// Digital circuit ALU(4-bit).dig as structural Verilog
module ALU_4_bit (
  input  [3:0] A_3_0,
  input  [3:0] B_3_0,
  input  [1:0] OP_1_0,
  output [3:0] R_3_0,
  output ZF,
  output CF
);

  wire [3:0] full_adder_4_bit_1_sum_3_0, ror_4_bit_1_o_3_0, xor_circuit_4_bit_1_o_3_0;

  XOR_Circuit_4_bit xor_circuit_4_bit_1 (.A_3_0(A_3_0), .B_3_0(B_3_0), .O_3_0(xor_circuit_4_bit_1_o_3_0));
  Full_Adder_4_bit full_adder_4_bit_1 (.A_3_0(A_3_0), .B_3_0(B_3_0), .Sum_3_0(full_adder_4_bit_1_sum_3_0), .Carry(CF));
  ROR_4_bit ror_4_bit_1 (.O_3_0(ror_4_bit_1_o_3_0), .A_3_0(A_3_0), .B_1_0(B_3_0[1:0]));
  nor nor_1 (ZF, R_3_0[0], R_3_0[1], R_3_0[2], R_3_0[3]);
  Multiplexer #(.Selector_Bits(2), .Bits(4)) multiplexer_1 (
    .sel(OP_1_0), .in_0(xor_circuit_4_bit_1_o_3_0), .in_1(full_adder_4_bit_1_sum_3_0),
    .in_2(ror_4_bit_1_o_3_0), .in_3(4'b0000), .out(R_3_0));
endmodule
