// Digital circuit CPU.dig as structural Verilog
module CPU (
  input  PC_Enable,
  input  CLK,
  input  Load,
  input  CLK_load,
  output [1:0] R_1,
  output [1:0] R_2,
  output [3:0] Operand_1,
  output [3:0] Operand_2,
  output [14:0] Loaded_Instruction,
  output [1:0] WR,
  output [1:0] OP,
  output [3:0] Result,
  output [3:0] RAM_Address,
  output [14:0] Instruction
);

  wire and_2_out, CLK_CPU, control_unit_1_imm_sel, control_unit_1_reg_en, JMP_SEL, or_1_out, ZF;
  wire [3:0] _0_to_5_counter_1_output, multiplexer_1_out, PC_Adder_output_3_0,
       register_set_4_4_bit_register_1_b_3_0;
  wire [14:0] ROM_d;

  and and_1 (CLK_CPU, PC_Enable, CLK);
  and and_2 (and_2_out, CLK_load, Load);
  Multiplexer #(.Bits(4)) multiplexer_1 (
    .sel(JMP_SEL), .in_0(PC_Adder_output_3_0), .in_1(Instruction[10:7]), .out(multiplexer_1_out));
  or or_1 (or_1_out, CLK, and_2_out);
  _0_to_5_counter _0_to_5_counter_1 (.Output(_0_to_5_counter_1_output), .CLK(and_2_out));
  Program_Counter program_counter_1 (.I_3_0(multiplexer_1_out), .CLK(CLK_CPU), .O_3_0(RAM_Address));
  PC_Adder PC_Adder (.Input(RAM_Address), .Output_3_0(PC_Adder_output_3_0));
  ROM #(.AddrBits(4), .Bits(15)) ROM (.A(_0_to_5_counter_1_output), .sel(Load), .D(ROM_d));
  RAM_10x15 ram_10x15_1 (
    .RA_1_3_0(RAM_Address), .RA_2_3_0(_0_to_5_counter_1_output), .WS_3_0(_0_to_5_counter_1_output),
    .WE(Load), .WD_14_0(ROM_d), .CLK(or_1_out), .RD_1_14_0(Instruction), .RD_2_14_0(Loaded_Instruction));
  Register_Set_4_4_bit_Register register_set_4_4_bit_register_1 (
    .Wr_1_0(Instruction[10:9]), .Wrd_3_0(Result), .CLK(CLK_CPU), .a_3_0(Operand_1),
    .b_3_0(register_set_4_4_bit_register_1_b_3_0), .Ra_1_0(Instruction[10:9]), .Rb_1_0(Instruction[8:7]),
    .EN_reg(control_unit_1_reg_en));
  ALU_4_bit alu_4_bit_1 (.A_3_0(Operand_1), .B_3_0(Operand_2), .OP_1_0(OP), .R_3_0(Result), .ZF(ZF));  // open: CF
  Control_Unit control_unit_1 (
    .OPCODE_3_0(Instruction[14:11]), .ZF(ZF), .OP_1_0(OP), .REG_EN(control_unit_1_reg_en),
    .IMM_SEL(control_unit_1_imm_sel), .JMP_SEL(JMP_SEL));
  Multiplexer #(.Bits(4)) multiplexer_2 (
    .sel(control_unit_1_imm_sel), .in_0(register_set_4_4_bit_register_1_b_3_0), .in_1(Instruction[8:5]),
    .out(Operand_2));

  assign R_1 = Instruction[10:9];
  assign R_2 = Instruction[8:7];
  assign WR = Instruction[10:9];

  // Other names for the same wires on the sheet: a[3:0] = Operand_1; b[3:0] = Operand_2; R[3:0] = Result;
  //   RA_1[3:0] = RAM_Address; RD_1[14:0] = Instruction; RD_2[14:0] = Loaded_Instruction

  // Notes on the sheet:
  //   Load: This Load Button Just Loads the Assembly Code from Rom to RAM in second cycle. 
  //   In first cycle it does nothing..
  //   THIS ASSEMBLY CODE IS UPLOADED TO ROM
  //   XOR R1, R1 _____________(000001010000000)
  //   ADD R1, 5 ______________(010101010100000)
  //   ROR R1, 3 ______________(011001001100000)
  //   JMP JMP_TO ____________(100001010000000 )
  //   JMP_XOR: XOR R1, R1 ____(000001010000000)
  //   JMP_TO: JNZ JMP_XOR ___(100101000000000)
  //   EXIT:
  //   Register Mode(Type of OP = 00)  = 2 bit(Type of OP) + 2 bit(OP) + 2 bit(Address of R1) + 2 bit(Address of R2) + 7 bit(Unused)
  //   Immediate Mode(Type of OP = 01) = 2 bit(Type of OP) + 2 bit(OP) + 2 bit(Address of R1) + 4 bit(Immediate Value) + 5 bit(Unused)
  //   OP:
  //   __________XOR = 00
  //   __________ADD = 01
  //   __________ROR = 10
  //   Branching(Type of OP = 10) =  2 bit(Type of OP) + 2 bit(OP) + 4 bit(Jump Address) + 7 bit(Unused)
  //   OP:	
  //   __________JMP = 00
  //   __________JNZ = 01
  //   contents of ROM (hex, n*v repeats v):
  //   280,2aa0,3260,4280,280,4a00
endmodule
