// Digital circuit Control Unit.dig as structural Verilog
module Control_Unit (
  input  [3:0] OPCODE_3_0,
  input  ZF,
  output [1:0] OP_1_0,
  output IMM_SEL,
  output REG_EN,
  output JMP_SEL
);

  wire and_2_out, and_3_out, and_4_out, and_5_out, or_1_out;

  and and_1 (IMM_SEL, OPCODE_3_0[2], ~OPCODE_3_0[3]);  // And
  and and_2 (and_2_out, ~OPCODE_3_0[0], ~OPCODE_3_0[1]);  // And
  and and_3 (and_3_out, OPCODE_3_0[0], ~OPCODE_3_0[1]);  // And
  and and_4 (and_4_out, and_3_out, ~ZF);  // And
  not not_1 (REG_EN, OPCODE_3_0[3]);
  and and_5 (and_5_out, OPCODE_3_0[3], ~OPCODE_3_0[2]);  // And
  or or_1 (or_1_out, and_2_out, and_4_out);
  and and_6 (JMP_SEL, and_5_out, or_1_out);

  assign OP_1_0 = OPCODE_3_0[1:0];
endmodule
