// Digital circuit Flag Register.dig as structural Verilog
module Flag_Register (
  input  CF_i,
  input  ZF_i,
  input  CLK,
  output CF_o,
  output ZF_o
);

  Register_1_bit register_1_bit_1 (.D_in(CF_i), .SEL(1'b1), .CLK(CLK), .D_out(CF_o));
  Register_1_bit register_1_bit_2 (.D_in(ZF_i), .SEL(1'b1), .CLK(CLK), .D_out(ZF_o));
endmodule
