// Digital circuit Full Adder(4 bit).dig as structural Verilog
module Full_Adder_4_bit (
  input  [3:0] A_3_0,
  input  [3:0] B_3_0,
  output [3:0] Sum_3_0,
  output Carry
);

  wire full_adder_building_block_2_c_out, full_adder_building_block_3_c_out,
       full_adder_building_block_4_c_out;

  Full_Adder_building_Block full_adder_building_block_1 (
    .B(B_3_0[3]), .A(A_3_0[3]), .S(Sum_3_0[3]), .C_out(Carry), .C_in(full_adder_building_block_2_c_out));
  Full_Adder_building_Block full_adder_building_block_2 (
    .B(B_3_0[2]), .A(A_3_0[2]), .S(Sum_3_0[2]), .C_out(full_adder_building_block_2_c_out),
    .C_in(full_adder_building_block_3_c_out));
  Full_Adder_building_Block full_adder_building_block_3 (
    .B(B_3_0[1]), .A(A_3_0[1]), .S(Sum_3_0[1]), .C_out(full_adder_building_block_3_c_out),
    .C_in(full_adder_building_block_4_c_out));
  Full_Adder_building_Block full_adder_building_block_4 (
    .B(B_3_0[0]), .A(A_3_0[0]), .S(Sum_3_0[0]), .C_out(full_adder_building_block_4_c_out), .C_in(1'b0));

  // Other names for the same wires on the sheet: A[3:0] = A_3_0; B[3:0] = B_3_0
endmodule
