// Digital circuit PC Adder.dig as structural Verilog
module PC_Adder (
  input  [3:0] Input,
  output [3:0] Output_3_0
);

  Full_Adder_4_bit full_adder_4_bit_1 (.A_3_0(4'b0001), .B_3_0(Input), .Sum_3_0(Output_3_0));  // open: Carry
endmodule
