// Digital circuit Program Counter.dig as structural Verilog
module Program_Counter (
  input  [3:0] I_3_0,
  input  CLK,
  output [3:0] O_3_0
);

  Register_4_bit register_4_bit_1 (.D_in(I_3_0), .SEL(1'b1), .CLK(CLK), .D_out(O_3_0));
endmodule
