// Digital circuit RAM(10x15).dig as structural Verilog
module RAM_10x15 (
  input  [14:0] WD_14_0,
  input  CLK,
  input  [3:0] WS_3_0,
  input  [3:0] RA_2_3_0,
  input  [3:0] RA_1_3_0,
  input  WE,
  output [14:0] RD_1_14_0,
  output [14:0] RD_2_14_0
);

  wire and_1_out, and_2_out, and_3_out, and_4_out, and_5_out, and_6_out, and_7_out, and_8_out, and_9_out,
       and_10_out, RS_1_0, RS_1_1, RS_1_2, RS_1_3, RS_1_4, RS_1_5, RS_1_6, RS_1_7, RS_1_8, RS_1_9, RS_2_0,
       RS_2_1, RS_2_2, RS_2_3, RS_2_4, RS_2_5, RS_2_6, RS_2_7, RS_2_8, RS_2_9, WS_0, WS_1, WS_2, WS_3, WS_4,
       WS_5, WS_6, WS_7, WS_8, WS_9;
  wire [14:0] RD_1_0, RD_1_1, RD_1_2, RD_1_3, RD_1_4, RD_1_5, RD_1_6, RD_1_7, RD_1_8, RD_1_9, RD_2_0, RD_2_1,
       RD_2_2, RD_2_3, RD_2_4, RD_2_5, RD_2_6, RD_2_7, RD_2_8, RD_2_9;

  Decoder #(.Selector_Bits(4)) decoder_1 (
    .sel(RA_1_3_0), .out_0(RS_1_0), .out_1(RS_1_1), .out_2(RS_1_2), .out_3(RS_1_3), .out_4(RS_1_4),
    .out_5(RS_1_5), .out_6(RS_1_6), .out_7(RS_1_7), .out_8(RS_1_8), .out_9(RS_1_9));  // open: out_10, out_11, out_12, out_13, out_14, out_15
  Decoder #(.Selector_Bits(4)) decoder_2 (
    .sel(RA_2_3_0), .out_0(RS_2_0), .out_1(RS_2_1), .out_2(RS_2_2), .out_3(RS_2_3), .out_4(RS_2_4),
    .out_5(RS_2_5), .out_6(RS_2_6), .out_7(RS_2_7), .out_8(RS_2_8), .out_9(RS_2_9));  // open: out_10, out_11, out_12, out_13, out_14, out_15
  Decoder #(.Selector_Bits(4)) decoder_3 (
    .sel(WS_3_0), .out_0(WS_0), .out_1(WS_1), .out_2(WS_2), .out_3(WS_3), .out_4(WS_4), .out_5(WS_5),
    .out_6(WS_6), .out_7(WS_7), .out_8(WS_8), .out_9(WS_9));  // open: out_10, out_11, out_12, out_13, out_14, out_15
  and and_1 (and_1_out, WS_0, WE);
  and and_2 (and_2_out, WS_1, WE);
  and and_3 (and_3_out, WS_2, WE);
  and and_4 (and_4_out, WS_3, WE);
  and and_5 (and_5_out, WS_4, WE);
  and and_6 (and_6_out, WS_5, WE);
  and and_7 (and_7_out, WS_6, WE);
  and and_8 (and_8_out, WS_7, WE);
  and and_9 (and_9_out, WS_8, WE);
  and and_10 (and_10_out, WS_9, WE);
  RAM_1x15 ram_1x15_1 (
    .RD_1_14_0(RD_1_0), .RD_2_14_0(RD_2_0), .RS_1(RS_1_0), .RS_2(RS_2_0), .WS(and_1_out), .WD_14_0(WD_14_0),
    .CLK(CLK));
  RAM_1x15 ram_1x15_2 (
    .RD_1_14_0(RD_1_1), .RD_2_14_0(RD_2_1), .RS_1(RS_1_1), .RS_2(RS_2_1), .WS(and_2_out), .WD_14_0(WD_14_0),
    .CLK(CLK));
  RAM_1x15 ram_1x15_3 (
    .RD_1_14_0(RD_1_2), .RD_2_14_0(RD_2_2), .RS_1(RS_1_2), .RS_2(RS_2_2), .WS(and_3_out), .WD_14_0(WD_14_0),
    .CLK(CLK));
  RAM_1x15 ram_1x15_4 (
    .RD_1_14_0(RD_1_3), .RD_2_14_0(RD_2_3), .RS_1(RS_1_3), .RS_2(RS_2_3), .WS(and_4_out), .WD_14_0(WD_14_0),
    .CLK(CLK));
  RAM_1x15 ram_1x15_5 (
    .RD_1_14_0(RD_1_4), .RD_2_14_0(RD_2_4), .RS_1(RS_1_4), .RS_2(RS_2_4), .WS(and_5_out), .WD_14_0(WD_14_0),
    .CLK(CLK));
  RAM_1x15 ram_1x15_6 (
    .RD_1_14_0(RD_1_5), .RD_2_14_0(RD_2_5), .RS_1(RS_1_5), .RS_2(RS_2_5), .WS(and_6_out), .WD_14_0(WD_14_0),
    .CLK(CLK));
  RAM_1x15 ram_1x15_7 (
    .RD_1_14_0(RD_1_6), .RD_2_14_0(RD_2_6), .RS_1(RS_1_6), .RS_2(RS_2_6), .WS(and_7_out), .WD_14_0(WD_14_0),
    .CLK(CLK));
  RAM_1x15 ram_1x15_8 (
    .RD_1_14_0(RD_1_7), .RD_2_14_0(RD_2_7), .RS_1(RS_1_7), .RS_2(RS_2_7), .WS(and_8_out), .WD_14_0(WD_14_0),
    .CLK(CLK));
  RAM_1x15 ram_1x15_9 (
    .RD_1_14_0(RD_1_8), .RD_2_14_0(RD_2_8), .RS_1(RS_1_8), .RS_2(RS_2_8), .WS(and_9_out), .WD_14_0(WD_14_0),
    .CLK(CLK));
  RAM_1x15 ram_1x15_10 (
    .RD_1_14_0(RD_1_9), .RD_2_14_0(RD_2_9), .RS_1(RS_1_9), .RS_2(RS_2_9), .WS(and_10_out), .WD_14_0(WD_14_0),
    .CLK(CLK));
  assign RD_1_14_0 = RD_1_0 | RD_1_1 | RD_1_2 | RD_1_3 | RD_1_4 | RD_1_5 | RD_1_6 | RD_1_7 | RD_1_8 | RD_1_9;  // Or or_1, 15 bits wide
  assign RD_2_14_0 = RD_2_0 | RD_2_1 | RD_2_2 | RD_2_3 | RD_2_4 | RD_2_5 | RD_2_6 | RD_2_7 | RD_2_8 | RD_2_9;  // Or or_2, 15 bits wide
endmodule
