// Digital circuit RAM(1x1).dig as structural Verilog
module RAM_1x1 (
  input  WS,
  input  WD,
  input  CLK,
  input  RS1,
  input  RS2,
  output RD1,
  output RD2
);

  wire d_ff_1_q, multiplexer_1_out;

  Multiplexer multiplexer_1 (.sel(WS), .in_0(d_ff_1_q), .in_1(WD), .out(multiplexer_1_out));
  D_FF d_ff_1 (.D(multiplexer_1_out), .C(CLK), .Q(d_ff_1_q));  // open: nQ
  and and_1 (RD1, d_ff_1_q, RS1);
  and and_2 (RD2, d_ff_1_q, RS2);
endmodule
