// Digital circuit RAM(1x15).dig as structural Verilog
module RAM_1x15 (
  input  [14:0] WD_14_0,
  input  RS_1,
  input  RS_2,
  input  WS,
  input  CLK,
  output [14:0] RD_1_14_0,
  output [14:0] RD_2_14_0
);

  RAM_1x1 ram_1x1_1 (
    .WD(WD_14_0[14]), .WS(WS), .RS1(RS_1), .RS2(RS_2), .CLK(CLK), .RD1(RD_1_14_0[14]), .RD2(RD_2_14_0[14]));
  RAM_1x1 ram_1x1_2 (
    .WD(WD_14_0[13]), .WS(WS), .RS1(RS_1), .RS2(RS_2), .CLK(CLK), .RD1(RD_1_14_0[13]), .RD2(RD_2_14_0[13]));
  RAM_1x1 ram_1x1_3 (
    .WD(WD_14_0[12]), .WS(WS), .RS1(RS_1), .RS2(RS_2), .CLK(CLK), .RD1(RD_1_14_0[12]), .RD2(RD_2_14_0[12]));
  RAM_1x1 ram_1x1_4 (
    .WD(WD_14_0[11]), .WS(WS), .RS1(RS_1), .RS2(RS_2), .CLK(CLK), .RD1(RD_1_14_0[11]), .RD2(RD_2_14_0[11]));
  RAM_1x1 ram_1x1_5 (
    .WD(WD_14_0[10]), .WS(WS), .RS1(RS_1), .RS2(RS_2), .CLK(CLK), .RD1(RD_1_14_0[10]), .RD2(RD_2_14_0[10]));
  RAM_1x1 ram_1x1_6 (
    .WD(WD_14_0[9]), .WS(WS), .RS1(RS_1), .RS2(RS_2), .CLK(CLK), .RD1(RD_1_14_0[9]), .RD2(RD_2_14_0[9]));
  RAM_1x1 ram_1x1_7 (
    .WD(WD_14_0[8]), .WS(WS), .RS1(RS_1), .RS2(RS_2), .CLK(CLK), .RD1(RD_1_14_0[8]), .RD2(RD_2_14_0[8]));
  RAM_1x1 ram_1x1_8 (
    .WD(WD_14_0[7]), .WS(WS), .RS1(RS_1), .RS2(RS_2), .CLK(CLK), .RD1(RD_1_14_0[7]), .RD2(RD_2_14_0[7]));
  RAM_1x1 ram_1x1_9 (
    .WD(WD_14_0[6]), .WS(WS), .RS1(RS_1), .RS2(RS_2), .CLK(CLK), .RD1(RD_1_14_0[6]), .RD2(RD_2_14_0[6]));
  RAM_1x1 ram_1x1_10 (
    .WD(WD_14_0[5]), .WS(WS), .RS1(RS_1), .RS2(RS_2), .CLK(CLK), .RD1(RD_1_14_0[5]), .RD2(RD_2_14_0[5]));
  RAM_1x1 ram_1x1_11 (
    .WD(WD_14_0[4]), .WS(WS), .RS1(RS_1), .RS2(RS_2), .CLK(CLK), .RD1(RD_1_14_0[4]), .RD2(RD_2_14_0[4]));
  RAM_1x1 ram_1x1_12 (
    .WD(WD_14_0[3]), .WS(WS), .RS1(RS_1), .RS2(RS_2), .CLK(CLK), .RD1(RD_1_14_0[3]), .RD2(RD_2_14_0[3]));
  RAM_1x1 ram_1x1_13 (
    .WD(WD_14_0[2]), .WS(WS), .RS1(RS_1), .RS2(RS_2), .CLK(CLK), .RD1(RD_1_14_0[2]), .RD2(RD_2_14_0[2]));
  RAM_1x1 ram_1x1_14 (
    .WD(WD_14_0[1]), .WS(WS), .RS1(RS_1), .RS2(RS_2), .CLK(CLK), .RD1(RD_1_14_0[1]), .RD2(RD_2_14_0[1]));
  RAM_1x1 ram_1x1_15 (
    .WD(WD_14_0[0]), .WS(WS), .RS1(RS_1), .RS2(RS_2), .CLK(CLK), .RD1(RD_1_14_0[0]), .RD2(RD_2_14_0[0]));
endmodule
