// Digital circuit ROR(4-bit).dig as structural Verilog
module ROR_4_bit (
  input  [1:0] B_1_0,
  input  [3:0] A_3_0,
  output [3:0] O_3_0
);

  Multiplexer #(.Selector_Bits(2)) multiplexer_1 (
    .sel(B_1_0), .in_0(A_3_0[3]), .in_1(A_3_0[0]), .in_2(A_3_0[1]), .in_3(A_3_0[2]), .out(O_3_0[3]));
  Multiplexer #(.Selector_Bits(2)) multiplexer_2 (
    .sel(B_1_0), .in_0(A_3_0[2]), .in_1(A_3_0[3]), .in_2(A_3_0[0]), .in_3(A_3_0[1]), .out(O_3_0[2]));
  Multiplexer #(.Selector_Bits(2)) multiplexer_3 (
    .sel(B_1_0), .in_0(A_3_0[1]), .in_1(A_3_0[2]), .in_2(A_3_0[3]), .in_3(A_3_0[0]), .out(O_3_0[1]));
  Multiplexer #(.Selector_Bits(2)) multiplexer_4 (
    .sel(B_1_0), .in_0(A_3_0[0]), .in_1(A_3_0[1]), .in_2(A_3_0[2]), .in_3(A_3_0[3]), .out(O_3_0[0]));

  // Other names for the same wires on the sheet: A_0 = A_3_0[0]; A_1 = A_3_0[1]; A_2 = A_3_0[2]; A_3 = A_3_0[3]
endmodule
