// Digital circuit Register Set(4 4-bit Register).dig as structural Verilog
module Register_Set_4_4_bit_Register (
  input  CLK,
  input  [3:0] Wrd_3_0,
  input  [1:0] Wr_1_0,
  input  [1:0] Ra_1_0,
  input  [1:0] Rb_1_0,
  input  EN_reg,
  output [3:0] a_3_0,
  output [3:0] b_3_0
);

  wire and_1_out, and_2_out, and_3_out, and_4_out, decoder_1_out_0, decoder_1_out_1, decoder_1_out_2,
       decoder_1_out_3;
  wire [3:0] D_out_0, D_out_1, D_out_2, D_out_3;

  Decoder #(.Selector_Bits(2)) decoder_1 (
    .sel(Wr_1_0), .out_0(decoder_1_out_0), .out_1(decoder_1_out_1), .out_2(decoder_1_out_2),
    .out_3(decoder_1_out_3));
  and and_1 (and_1_out, decoder_1_out_0, EN_reg);
  and and_2 (and_2_out, decoder_1_out_1, EN_reg);
  and and_3 (and_3_out, decoder_1_out_2, EN_reg);
  and and_4 (and_4_out, decoder_1_out_3, EN_reg);
  Register_4_bit register_4_bit_1 (.D_in(Wrd_3_0), .SEL(and_1_out), .CLK(CLK), .D_out(D_out_0));
  Register_4_bit register_4_bit_2 (.D_in(Wrd_3_0), .SEL(and_2_out), .CLK(CLK), .D_out(D_out_1));
  Register_4_bit register_4_bit_3 (.D_in(Wrd_3_0), .SEL(and_3_out), .CLK(CLK), .D_out(D_out_2));
  Register_4_bit register_4_bit_4 (.D_in(Wrd_3_0), .SEL(and_4_out), .CLK(CLK), .D_out(D_out_3));
  Multiplexer #(.Bits(4), .Selector_Bits(2)) multiplexer_1 (
    .sel(Ra_1_0), .in_0(D_out_0), .in_1(D_out_1), .in_2(D_out_2), .in_3(D_out_3), .out(a_3_0));
  Multiplexer #(.Selector_Bits(2), .Bits(4)) multiplexer_2 (
    .sel(Rb_1_0), .in_0(D_out_0), .in_1(D_out_1), .in_2(D_out_2), .in_3(D_out_3), .out(b_3_0));

  // Other names for the same wires on the sheet: a[3:0] = a_3_0; b[3:0] = b_3_0; Ra[1:0] = Ra_1_0; Rb[1:0] = Rb_1_0;
  //   REG_EN = EN_reg
endmodule
