// Digital circuit Register(1-bit).dig as structural Verilog
module Register_1_bit (
  input  D_in,
  input  SEL,
  input  CLK,
  output D_out
);

  wire multiplexer_1_out;

  Multiplexer multiplexer_1 (.sel(SEL), .in_0(D_out), .in_1(D_in), .out(multiplexer_1_out));
  D_FF d_ff_1 (.D(multiplexer_1_out), .C(CLK), .Q(D_out));  // open: nQ
endmodule
