// Digital circuit Register(4-bit).dig as structural Verilog
module Register_4_bit (
  input  [3:0] D_in,
  input  SEL,
  input  CLK,
  output [3:0] D_out
);

  Register_1_bit register_1_bit_1 (.D_in(D_in[0]), .SEL(SEL), .CLK(CLK), .D_out(D_out[0]));
  Register_1_bit register_1_bit_2 (.D_in(D_in[1]), .SEL(SEL), .CLK(CLK), .D_out(D_out[1]));
  Register_1_bit register_1_bit_3 (.D_in(D_in[2]), .SEL(SEL), .CLK(CLK), .D_out(D_out[2]));
  Register_1_bit register_1_bit_4 (.D_in(D_in[3]), .SEL(SEL), .CLK(CLK), .D_out(D_out[3]));
endmodule
