// Digital circuit test_control_unit.dig as structural Verilog
module test_control_unit (
  input  [3:0] OPCODE_3_0,
  input  ZF,
  output [1:0] OP_1_0,
  output IMM_SEL,
  output REG_EN,
  output JMP_SEL
);

  wire and_2_out, and_3_out, and_4_out, and_5_out, or_1_out;

  and and_1 (IMM_SEL, OPCODE_3_0[2], ~OPCODE_3_0[3]);  // And
  and and_2 (and_2_out, ~OPCODE_3_0[0], ~OPCODE_3_0[1]);  // And
  and and_3 (and_3_out, OPCODE_3_0[0], ~OPCODE_3_0[1]);  // And
  and and_4 (and_4_out, and_3_out, ~ZF);  // And
  not not_1 (REG_EN, OPCODE_3_0[3]);
  and and_5 (and_5_out, OPCODE_3_0[3], ~OPCODE_3_0[2]);  // And
  or or_1 (or_1_out, and_2_out, and_4_out);
  and and_6 (JMP_SEL, and_5_out, or_1_out);

  assign OP_1_0 = OPCODE_3_0[1:0];
endmodule

/* Test case:
OPCODE[3:0] ZF OP[1:0] IMM_SEL REG_EN JMP_SEL
# Register-Register ALU operations (0x0 to 0x2)
0 0 0 0 1 0
0 1 0 0 1 0
1 0 1 0 1 0
1 1 1 0 1 0
2 0 2 0 1 0
2 1 2 0 1 0

# Immediate ALU operations (0x4 to 0x6)
4 0 0 1 1 0
4 1 0 1 1 0
5 0 1 1 1 0
5 1 1 1 1 0
6 0 2 1 1 0
6 1 2 1 1 0

# Jump Unconditional (0x8)
8 0 0 0 0 1
8 1 0 0 0 1

# Jump if Not Zero (0x9): jumps when ZF=0, does not jump when ZF=1
9 0 1 0 0 1
9 1 1 0 0 0
*/
